# Fritzing sketch fritzing sketch (saved by Fritzing 1.0.5)

parts:
  U1 = LuaNode32 / ESP32 [part_number=ESP32S-PIN30]
  S1 = Pushbutton [package="[SMD]"]
  S2 = Pushbutton [package="[SMD]"]
  J1 = Basic Servo
  J2 = Basic Servo
  J3 = Basic Servo
  U2 = POT [knob_status=50% power=0.5W package=pot_mammoth]
  U3 = POT [knob_status=50% power=0.5W package=pot_mammoth]

nets:
  N1: U1.D32, U2.A
  N2: U1.D33, U3.A
  N3: U1.D12, S2.Pin_2
  N4: U1.D13, S1.Pin_2
  N5: U1.3V3, U2.S
  N6: U1.RX2, J1.pulse
  N7: U1.TX2, J2.pulse
  N8: U1.D18, J3.pulse

custom parts:
  LuaNode32 / ESP32: New Image for LuaNode32 DOIT ESP32 DEVKIT V1. Base parts from LuaNode32 / ESP32 ESP32 based LuaNode32 by G.Noorlander DOIT Esp32 DevKit v1 (30 pins long, 11 pins width) by Werner Rothschopf (modified by vanepp Dec 2018)
